// Logisim project add16.circ as structural Verilog: 1 circuit, main circuit main
module main (
  input  a1,
  input  in_2,
  input  a2,
  input  in_4,
  input  a4,
  input  in_6,
  input  a8,
  input  in_8,
  input  a16,
  input  in_10,
  input  a32,
  input  in_12,
  input  a64,
  input  in_14,
  input  a128,
  input  in_16,
  input  a256,
  input  in_18,
  input  a512,
  input  in_20,
  input  a1024,
  input  in_22,
  input  a2048,
  input  in_24,
  input  a4096,
  input  in_26,
  input  a8192,
  input  in_28,
  input  a16384,
  input  in_30,
  input  aneg,
  input  in_32,
  output out_33,
  output out_34,
  output out_35,
  output out_36,
  output out_37,
  output out_38,
  output out_39,
  output out_40,
  output out_41,
  output out_42,
  output out_43,
  output out_44,
  output out_45,
  output out_46,
  output out_47,
  output out_48
);

  wire adder_1_cout, adder_2_cout, adder_3_cout, adder_4_cout, adder_5_cout, adder_6_cout, adder_7_cout,
       adder_8_cout, adder_9_cout, adder_10_cout, adder_11_cout, adder_12_cout, adder_13_cout, adder_14_cout,
       adder_15_cout;

  Adder #(.width(1)) adder_1 (.a(a1), .b(in_2), .out(out_33), .cout(adder_1_cout));  // open: cin
  Adder #(.width(1)) adder_2 (.a(a2), .b(in_4), .out(out_34), .cin(adder_1_cout), .cout(adder_2_cout));
  Adder #(.width(1)) adder_3 (.a(a4), .b(in_6), .out(out_35), .cin(adder_2_cout), .cout(adder_3_cout));
  Adder #(.width(1)) adder_4 (.a(a8), .b(in_8), .out(out_36), .cin(adder_3_cout), .cout(adder_4_cout));
  Adder #(.width(1)) adder_5 (.a(a16), .b(in_10), .out(out_37), .cin(adder_4_cout), .cout(adder_5_cout));
  Adder #(.width(1)) adder_6 (.a(a32), .b(in_12), .out(out_38), .cin(adder_5_cout), .cout(adder_6_cout));
  Adder #(.width(1)) adder_7 (.a(a64), .b(in_14), .out(out_39), .cin(adder_6_cout), .cout(adder_7_cout));
  Adder #(.width(1)) adder_8 (.a(a128), .b(in_16), .out(out_40), .cin(adder_7_cout), .cout(adder_8_cout));
  Adder #(.width(1)) adder_9 (.a(a256), .b(in_18), .out(out_41), .cin(adder_8_cout), .cout(adder_9_cout));
  Adder #(.width(1)) adder_10 (.a(a512), .b(in_20), .out(out_42), .cin(adder_9_cout), .cout(adder_10_cout));
  Adder #(.width(1)) adder_11 (.a(a1024), .b(in_22), .out(out_43), .cin(adder_10_cout), .cout(adder_11_cout));
  Adder #(.width(1)) adder_12 (.a(a2048), .b(in_24), .out(out_44), .cin(adder_11_cout), .cout(adder_12_cout));
  Adder #(.width(1)) adder_13 (.a(a4096), .b(in_26), .out(out_45), .cin(adder_12_cout), .cout(adder_13_cout));
  Adder #(.width(1)) adder_14 (.a(a8192), .b(in_28), .out(out_46), .cin(adder_13_cout), .cout(adder_14_cout));
  Adder #(.width(1)) adder_15 (.a(a16384), .b(in_30), .out(out_47), .cin(adder_14_cout), .cout(adder_15_cout));
  Adder #(.width(1)) adder_16 (.a(aneg), .b(in_32), .out(out_48), .cin(adder_15_cout));  // open: cout
endmodule
